# Fritzing sketch schemat-podlaczenia (saved by Fritzing 0.9.2b)
breadboards: 1

parts:
  Raspberry_Pi1 = Raspberry Pi 2
  LCD1 = LCD screen
  U1 = POT [package=pot_mammoth]

nets:
  N1: Raspberry_Pi1.GPIO17, LCD1.E
  N2: Raspberry_Pi1.3V3, LCD1.RS
  N3: Raspberry_Pi1.GPIO25, LCD1.DB4
  N4: Raspberry_Pi1.GPIO24, LCD1.DB7
  N5: Raspberry_Pi1.GPIO23, LCD1.DB6
  N6: Raspberry_Pi1.GPIO18, LCD1.DB5
  GND: Raspberry_Pi1.GND, LCD1.VSS, LCD1.R/W, LCD1.LED-, U1.S
  5V: Raspberry_Pi1.5V, LCD1.VDD, LCD1.LED+, U1.E
  N7: LCD1.V0, U1.A
